# Fritzing sketch CarronhoSchema (saved by Fritzing 0.9.6b)
breadboards: 1

parts:
  Part1 = Arduino Uno (Rev3)
  M1 = gear-motor
  M2 = gear-motor
  HC-SR04_Sensor_1 = HC-SR04 Ultrasonic Distance Sensor
  R1 = Resistor [tolerance=±5% resistance=220 package="0603 [SMD]"]
  LED1 = smd LED [color="Red (633nm)" package="0805 [SMD]"]  # not connected
  A1 = Pololu DRV 8833 Dual Motor Driver Carrier [part_number=DRV8833]
  VCC2 = 4 x AAA Battery Mount
  BAT1 = BC9VPC [package=bc9vpc]  # not connected

nets:
  N1: Part1.D9_PWM, A1.Pin_4
  N2: Part1.D10_PWM/SS, A1.Pin_3
  N3: Part1.D13/SCK, HC-SR04_Sensor_1.TRIG
  GND: Part1.GND, HC-SR04_Sensor_1.GND
  N4: Part1.D2, R1.Pin_0
  N5: Part1.D5_PWM, A1.Pin_6
  N6: Part1.D6_PWM, A1.Pin_5
  5V: Part1.5V, HC-SR04_Sensor_1.VCC
  N7: M1.pin_2, A1.Pin_13
  N8: M2.pin_1, A1.Pin_12
  N9: M2.pin_2, A1.Pin_11
  N10: A1.Pin_1, A1.Pin_16, VCC2.-
  N11: A1.Pin_2, VCC2.+
